// Logisim project ALU.circ as structural Verilog: 2 circuits, main circuit ALU_4
module ALU_4 (
  input  Carry_in,
  input  [3:0] a,
  input  [3:0] b,
  input  [2:0] sel,
  output [3:0] out_5,
  output Carry_out
);

  wire alu_1_carry_out, alu_2_carry_out, alu_3_carry_out;

  ALU alu_1 (.S(out_5[0]), .sel(sel), .a(a[0]), .b(b[0]), .Carry_in(Carry_in), .Carry_out(alu_1_carry_out));
  ALU alu_2 (.S(out_5[1]), .sel(sel), .a(a[1]), .b(b[1]), .Carry_in(alu_1_carry_out), .Carry_out(alu_2_carry_out));
  ALU alu_3 (.S(out_5[2]), .sel(sel), .a(a[2]), .b(b[2]), .Carry_in(alu_2_carry_out), .Carry_out(alu_3_carry_out));
  ALU alu_4 (.S(out_5[3]), .sel(sel), .a(a[3]), .b(b[3]), .Carry_in(alu_3_carry_out), .Carry_out(Carry_out));
endmodule

module ALU (
  input  a,
  input  b,
  input  Carry_in,
  input  [2:0] sel,
  output Carry_out,
  output S
);

  wire and_1_out, fulladder_1_s, not_1_out, or_1_out;

  FullAdder fulladder_1 (.Carry_in(Carry_in), .a(a), .b(b), .S(fulladder_1_s), .Carry_out(Carry_out));
  or or_1 (or_1_out, a, b);
  and and_1 (and_1_out, a, b);
  not not_1 (not_1_out, b);
  Mux_8_1 mux_8_1_1 (
    .in_1(fulladder_1_s), .in_2(or_1_out), .in_3(and_1_out), .in_4(not_1_out), .in_9(sel), .out_10(S));  // open: in_5, in_6, in_7, in_8
endmodule
