// Logisim project CPU_V1.circ as structural Verilog: 10 circuits, main circuit main
module main (
);

  wire button_1_out, uc_1_p5, uc_1_p6, uc_1_p7, uc_1_p8;
  wire [2:0] uc_1_p9;
  wire [3:0] main_1_p1, main_1_p5, main_1_p6, uc_1_p3, uc_1_p4;
  wire [11:0] rom_1_data;

  ROM #(.addrWidth(4), .dataWidth(12)) rom_1 (.addr(uc_1_p3), .data(rom_1_data), .sel(1'b1));
  Button button_1 (.out(button_1_out));
  // UC uc_1: pin names not known; wires that end beside it: rom_1_data, button_1_out, uc_1_p3, uc_1_p4, uc_1_p5, uc_1_p6, uc_1_p7, uc_1_p8, uc_1_p9
  PC pc_1 (.In(uc_1_p4), .out_2(uc_1_p3));
  // RegFile_main main_1: pin names not known; wires that end beside it: main_1_p1, uc_1_p5, uc_1_p7, uc_1_p8, main_1_p5, main_1_p6
  ALU_4 alu_4_1 (.in_1(main_1_p6), .in_2(main_1_p5), .out_4(main_1_p1), .in_3(uc_1_p9));
endmodule

module XOR (
  input  a,
  input  b,
  output S
);

  wire and_1_out, and_2_out, not_1_out, not_2_out;

  not not_1 (not_1_out, b);
  not not_2 (not_2_out, a);
  and and_1 (and_1_out, not_1_out, a);
  and and_2 (and_2_out, not_2_out, b);
  or or_1 (S, and_1_out, and_2_out);
endmodule

module HalfAdder (
  input  a,
  input  b,
  output Result,
  output Carry_out
);

  XOR xor_1 (.a(b), .S(Result), .b(a));
  and and_1 (Carry_out, b, a);
endmodule

module FullAdder (
  input  Carry_in,
  input  a,
  input  b,
  output S,
  output Carry_out
);

  wire halfadder_1_carry_out, halfadder_1_result, halfadder_2_carry_out;

  HalfAdder halfadder_1 (.Result(halfadder_1_result), .Carry_out(halfadder_1_carry_out), .a(b), .b(a));
  HalfAdder halfadder_2 (.Result(S), .Carry_out(halfadder_2_carry_out), .a(halfadder_1_result), .b(Carry_in));
  or or_1 (Carry_out, halfadder_2_carry_out, halfadder_1_carry_out);
endmodule

module Mux_2_1 (
  input  a,
  input  b,
  input  sel,
  output S
);

  wire and_1_out, and_2_out, not_1_out;

  not not_1 (not_1_out, sel);
  and and_1 (and_1_out, a, not_1_out);
  and and_2 (and_2_out, sel, b);
  or or_1 (S, and_1_out, and_2_out);
endmodule

module Mux_4_1 (
  input  a,
  input  b,
  input  c,
  input  d,
  input  [1:0] sel1,
  output S
);

  wire mux_2_1_1_s, mux_2_1_2_s;

  Mux_2_1 mux_2_1_1 (.a(a), .b(b), .S(mux_2_1_1_s), .sel(sel1[0]));
  Mux_2_1 mux_2_1_2 (.a(c), .b(d), .S(mux_2_1_2_s), .sel(sel1[0]));
  Mux_2_1 mux_2_1_3 (.a(mux_2_1_1_s), .b(mux_2_1_2_s), .S(S), .sel(sel1[1]));
endmodule

module Mux_8_1 (
  input  in_1,
  input  in_2,
  input  in_3,
  input  in_4,
  input  in_5,
  input  in_6,
  input  in_7,
  input  in_8,
  input  [2:0] in_9,
  output out_10
);

  wire mux_4_1_1_s, mux_4_1_2_s;

  Mux_4_1 mux_4_1_1 (.a(in_1), .b(in_2), .c(in_3), .d(in_4), .S(mux_4_1_1_s), .sel1(in_9[1:0]));
  Mux_4_1 mux_4_1_2 (.a(in_5), .b(in_6), .c(in_7), .d(in_8), .S(mux_4_1_2_s), .sel1(in_9[1:0]));
  Mux_2_1 mux_2_1_1 (.a(mux_4_1_1_s), .b(mux_4_1_2_s), .S(out_10), .sel(in_9[2]));
endmodule

module ALU (
  input  in_1,
  input  in_2,
  input  in_3,
  input  [2:0] in_4,
  output out_5,
  output out_6
);

  wire and_1_out, fulladder_1_s, not_1_out, or_1_out;

  FullAdder fulladder_1 (.a(in_2), .b(in_3), .Carry_in(in_1), .S(fulladder_1_s), .Carry_out(out_5));
  or or_1 (or_1_out, in_2, in_3);
  and and_1 (and_1_out, in_2, in_3);
  not not_1 (not_1_out, in_3);
  Mux_8_1 mux_8_1_1 (
    .in_1(fulladder_1_s), .in_2(or_1_out), .in_3(and_1_out), .in_4(not_1_out), .in_9(in_4), .out_10(out_6));  // open: in_5, in_6, in_7, in_8
endmodule

module ALU_4 (
  input  [3:0] in_1,
  input  [3:0] in_2,
  input  [2:0] in_3,
  output [3:0] out_4
);

  wire alu_1_out_5, alu_2_out_5, alu_3_out_5;

  ALU alu_1 (.out_5(alu_1_out_5), .out_6(out_4[0]), .in_2(in_1[0]), .in_3(in_2[0]), .in_1(1'b0), .in_4(in_3));
  ALU alu_2 (.out_5(alu_2_out_5), .out_6(out_4[1]), .in_2(in_1[1]), .in_3(in_2[1]), .in_1(alu_1_out_5), .in_4(in_3));
  ALU alu_3 (.out_5(alu_3_out_5), .out_6(out_4[2]), .in_2(in_1[2]), .in_3(in_2[2]), .in_1(alu_2_out_5), .in_4(in_3));
  ALU alu_4 (.out_6(out_4[3]), .in_2(in_1[3]), .in_3(in_2[3]), .in_1(alu_3_out_5), .in_4(in_3));  // open: out_5
endmodule

module PC (
  input  [3:0] In,
  output [3:0] out_2
);

  Reg_4 reg_4_1 (.in_1(In), .out_4(out_2), .in_3(1'b1));  // open: in_2
endmodule
