// Logisim project UC.circ as structural Verilog: 4 circuits, main circuit UC
module UC (
  input  [9:0] in_1,
  input  RESET,
  input  [3:0] PCIn,
  output [9:0] out_4,
  output wA,
  output wB,
  output wC,
  output wD,
  output rA1,
  output rA2,
  output rB1,
  output rB2,
  output rC1,
  output rC2,
  output rD1,
  output rD2,
  output [3:0] PCOut,
  output wPC,
  output [3:0] AD0,
  output wAD,
  output [2:0] function_sel
);

  PCSel pcsel_1 (.in_1(PCIn), .PCOut(PCOut), .reset(RESET));
  Clock clock_1 (.out(wPC));
  function_sel function_sel_1 ();  // open: in_1, out_2
  registerSelector registerselector_1 (.A(rA1), .B(rB1), .C(rC1), .D(rD1), .activate(1'b1));  // open: sel
  registerSelector registerselector_2 (.A(rA2), .B(rB2), .C(rC2), .D(rD2), .activate(1'b1));  // open: sel
  registerSelector registerselector_3 (.A(wA), .B(wB), .C(wC), .D(wD), .activate(1'b1));  // open: sel

  assign out_4 = in_1;
endmodule

module function_sel (
  input  [3:0] in_1,
  output [2:0] out_2
);

  wire not_1_out;

  and and_1 (out_2[0], in_1[0], not_1_out);
  not not_1 (not_1_out, in_1[2]);

  assign out_2[2:1] = in_1[2:1];
endmodule

module registerSelector (
  input  [1:0] sel,
  input  activate,
  output A,
  output B,
  output C,
  output D
);

  wire and_1_out, and_2_out, and_3_out, and_4_out, not_1_out, not_2_out, not_3_out, not_4_out;

  not not_1 (not_1_out, sel[0]);
  not not_2 (not_2_out, sel[1]);
  not not_3 (not_3_out, sel[0]);
  not not_4 (not_4_out, sel[1]);
  Mux_2_1 mux_2_1_1 (.a(1'b0), .b(and_1_out), .S(A), .sel(activate));
  and and_1 (and_1_out, not_1_out, not_2_out);
  Mux_2_1 mux_2_1_2 (.a(1'b0), .b(and_2_out), .S(B), .sel(activate));
  and and_2 (and_2_out, not_3_out, sel[1]);
  Mux_2_1 mux_2_1_3 (.a(1'b0), .b(and_3_out), .S(C), .sel(activate));
  and and_3 (and_3_out, sel[0], not_4_out);
  Mux_2_1 mux_2_1_4 (.a(1'b0), .b(and_4_out), .S(D), .sel(activate));
  and and_4 (and_4_out, sel[0], sel[1]);
endmodule

module PCSel (
  input  [3:0] in_1,
  input  reset,
  output [3:0] PCOut
);

  wire fulladder_1_carry_out, fulladder_2_carry_out, halfadder_1_carry_out, not_1_out;
  wire [3:0] halfadder_1_result;

  HalfAdder halfadder_1 (.Result(halfadder_1_result[0]), .Carry_out(halfadder_1_carry_out), .a(in_1[0]), .b(1'b1));
  FullAdder fulladder_1 (
    .Carry_in(halfadder_1_carry_out), .a(in_1[1]), .b(1'b0), .S(halfadder_1_result[1]),
    .Carry_out(fulladder_1_carry_out));
  FullAdder fulladder_2 (
    .Carry_in(fulladder_1_carry_out), .a(in_1[2]), .b(1'b0), .S(halfadder_1_result[2]),
    .Carry_out(fulladder_2_carry_out));
  FullAdder fulladder_3 (
    .Carry_in(fulladder_2_carry_out), .a(in_1[3]), .b(1'b0), .S(halfadder_1_result[3]));  // open: Carry_out
  Multiplexer #(.width(4), .disabled(0), .enable("false")) multiplexer_1 (
    .in0(4'b0000), .in1(halfadder_1_result), .out(PCOut), .sel(not_1_out));
  not not_1 (not_1_out, reset);
endmodule
