// Logisim project lib.circ as structural Verilog
module XOR (
  input  a,
  input  b,
  output S
);

  wire and_1_out, and_2_out, not_1_out, not_2_out;

  not not_1 (not_1_out, b);
  not not_2 (not_2_out, a);
  and and_1 (and_1_out, not_1_out, a);
  and and_2 (and_2_out, not_2_out, b);
  or or_1 (S, and_1_out, and_2_out);
endmodule

module Mux_2_1 (
  input  a,
  input  b,
  input  sel,
  output S
);

  wire and_1_out, and_2_out, not_1_out;

  not not_1 (not_1_out, sel);
  and and_1 (and_1_out, a, not_1_out);
  and and_2 (and_2_out, sel, b);
  or or_1 (S, and_1_out, and_2_out);
endmodule

module Mux_4_1 (
  input  a,
  input  b,
  input  c,
  input  d,
  input  [1:0] sel1,
  output S
);

  wire mux_2_1_1_s, mux_2_1_2_s;

  Mux_2_1 mux_2_1_1 (.a(a), .b(b), .S(mux_2_1_1_s), .sel(sel1[0]));
  Mux_2_1 mux_2_1_2 (.a(c), .b(d), .S(mux_2_1_2_s), .sel(sel1[0]));
  Mux_2_1 mux_2_1_3 (.a(mux_2_1_1_s), .b(mux_2_1_2_s), .S(S), .sel(sel1[1]));
endmodule

module Mux_8_1 (
  input  in_1,
  input  in_2,
  input  in_3,
  input  in_4,
  input  in_5,
  input  in_6,
  input  in_7,
  input  in_8,
  input  [2:0] in_9,
  output out_10
);

  wire mux_4_1_1_s, mux_4_1_2_s;

  Mux_4_1 mux_4_1_1 (.a(in_1), .b(in_2), .c(in_3), .d(in_4), .S(mux_4_1_1_s), .sel1(in_9[1:0]));
  Mux_4_1 mux_4_1_2 (.a(in_5), .b(in_6), .c(in_7), .d(in_8), .S(mux_4_1_2_s), .sel1(in_9[1:0]));
  Mux_2_1 mux_2_1_1 (.a(mux_4_1_1_s), .b(mux_4_1_2_s), .S(out_10), .sel(in_9[2]));
endmodule

module HalfAdder (
  input  a,
  input  b,
  output Result,
  output Carry_out
);

  XOR xor_1 (.a(b), .b(a), .S(Result));
  and and_1 (Carry_out, b, a);
endmodule

module FullAdder (
  input  Carry_in,
  input  a,
  input  b,
  output S,
  output Carry_out
);

  wire halfadder_1_carry_out, halfadder_1_result, halfadder_2_carry_out;

  HalfAdder halfadder_1 (.Result(halfadder_1_result), .Carry_out(halfadder_1_carry_out), .a(a), .b(b));
  HalfAdder halfadder_2 (.Result(S), .Carry_out(halfadder_2_carry_out), .a(Carry_in), .b(halfadder_1_result));
  or or_1 (Carry_out, halfadder_2_carry_out, halfadder_1_carry_out);
endmodule

module Mux_2_2 (
  input  [1:0] in_1,
  input  [1:0] in_2,
  input  in_3,
  output [1:0] out_4
);

  Mux_2_1 mux_2_1_1 (.a(in_1[0]), .b(in_2[0]), .S(out_4[0]), .sel(in_3));
  Mux_2_1 mux_2_1_2 (.a(in_1[1]), .b(in_2[1]), .S(out_4[1]), .sel(in_3));
endmodule
